// Logisim project Fluminense.circ as structural Verilog: 5 circuits, main circuit ULA 
// ULA
module ULA (
  input  [2:0] OP_ULA,
  input  [7:0] A,
  input  [7:0] B,
  output Overflow,
  output Zero,
  output [7:0] Output
);

  wire adder_1_cout, subtractor_1_bout;
  wire [7:0] adder_1_out, and_1_out, not_1_out, not_2_out, not_3_out, or_2_out, subtractor_1_out, xor_1_out;

  or or_1 (Overflow, subtractor_1_bout, adder_1_cout);
  Adder adder_1 (.a(A), .b(B), .out(adder_1_out), .cout(adder_1_cout));  // open: cin
  Subtractor subtractor_1 (.a(A), .b(B), .out(subtractor_1_out), .bout(subtractor_1_bout));  // open: bin
  assign and_1_out = A & B;  // AND_Gate and_1, 8 bits wide
  assign not_1_out = ~and_1_out;  // NOT_Gate not_1, 8 bits wide
  assign or_2_out = A | B;  // OR_Gate or_2, 8 bits wide
  assign not_2_out = ~or_2_out;  // NOT_Gate not_2, 8 bits wide
  assign xor_1_out = A ^ B;  // XOR_Gate xor_1, 8 bits wide
  assign not_3_out = ~A;  // NOT_Gate not_3, 8 bits wide
  Comparator comparator_1 (.a(subtractor_1_out), .b({8{1'b0}}), .eq(Zero));  // open: gt, lt
  Multiplexer #(.select(3), .width(8)) multiplexer_1 (
    .in0(adder_1_out), .in1(subtractor_1_out), .in2(and_1_out), .in3(not_1_out), .in4(or_2_out),
    .in5(not_2_out), .in6(xor_1_out), .in7(not_3_out), .out(Output), .sel(OP_ULA));  // open: en
endmodule

// Banco
module Banco_de_Registradores (
  input  [7:0] Input,
  input  Clear,
  input  Esc_REG,
  input  Clock,
  input  [1:0] REG_1,
  input  [1:0] REG_2,
  output [7:0] REG_1_LIDO,
  output [7:0] REG_2_LIDO,
  output [7:0] REG_00,
  output [7:0] REG_01,
  output [7:0] REG_10,
  output [7:0] REG_11
);

  wire demultiplexer_1_out0, demultiplexer_1_out1, demultiplexer_1_out2;

  Demultiplexer #(.select(2)) demultiplexer_1 (
    .out0(demultiplexer_1_out0), .out1(demultiplexer_1_out1), .out2(demultiplexer_1_out2), .out3(Clear),
    .in(Esc_REG), .sel(REG_1));  // open: en
  Register register_1 (.D(Input), .en(demultiplexer_1_out0), .Q(REG_00), .clk(Clock), .clr(Clear));
  Register register_2 (.D(Input), .en(demultiplexer_1_out1), .Q(REG_01), .clk(Clock), .clr(Clear));
  Register register_3 (.D(Input), .en(demultiplexer_1_out2), .Q(REG_10), .clk(Clock), .clr(Clear));
  Register register_4 (.D(Input), .en(Clear), .Q(REG_11), .clk(Clock), .clr(Clear));
  Multiplexer #(.select(2), .width(8)) multiplexer_1 (
    .in0(REG_00), .in1(REG_01), .in2(REG_10), .in3(REG_11), .out(REG_1_LIDO), .sel(REG_1));  // open: en
  Multiplexer #(.select(2), .width(8)) multiplexer_2 (
    .in0(REG_00), .in1(REG_01), .in2(REG_10), .in3(REG_11), .out(REG_2_LIDO), .sel(REG_2));  // open: en
endmodule

// M.Dados
module \Memória_de_Dados  (
  input  [7:0] Dado_Lido,
  input  [7:0] Dado_a_ser_Escrito,
  input  [7:0] Seletor,
  input  Enable_Seletor,
  input  Load,
  input  Clear,
  input  Clock
);

  wire not_1_out;

  RAM ram_1 (.addr(Seletor), .data(Dado_Lido), .sel(Enable_Seletor), .clk(Clock), .ld(Load), .clr(Clear));
  assign Dado_Lido = Dado_a_ser_Escrito;  // Buffer buffer_1, 8 bits wide
  not not_1 (not_1_out, Load);
endmodule

// UNI.C
module Unidade_de_Controle (
  input  [3:0] in_1,
  output \Endereço ,
  output Jump,
  output Branch,
  output [1:0] MemtoReg,
  output [2:0] ULAOP,
  output MemWrite_MemRead,
  output ALUSrc,
  output RegWrite
);

  Multiplexer #(.select(4), .width(11), .enable("false")) multiplexer_1 (
    .in1({11{1'b0}}), .in2({11{1'b0}}), .in3({11{1'b0}}), .in4({11{1'b0}}), .in5({11{1'b0}}),
    .in6({11{1'b0}}), .in7({11{1'b0}}), .in8({11{1'b0}}), .in9({11{1'b0}}), .in10({11{1'b0}}),
    .in11({11{1'b0}}), .in12({11{1'b0}}), .in13({11{1'b0}}), .in14({11{1'b0}}),
    .out({RegWrite, ALUSrc, MemWrite_MemRead, ULAOP, MemtoReg, Branch, Jump, \Endereço }), .sel(in_1));  // open: in0, in15

  // Notes on the sheet:
  //   0000 ADD
  //   0001 ADDI
  //   0010 SUB
  //   0011 SUBI
  //   0100 BEQ
  //   0101 JUMP
  //   0110 SW
  //   0111 LW
  //   1000 AND
  //   1001 NAND
  //   1010 OR
  //   1011 NOR
  //   1100 XOR
  //   1101 NOT
endmodule

module CPU (
  input  [7:0] REG_00,
  input  [7:0] REG_01,
  input  [7:0] REG_10,
  input  [7:0] REG_11,
  input  [7:0] ULA_A,
  input  [7:0] ULA_B,
  input  [7:0] ULA_S,
  input  [2:0] OpULA,
  input  [7:0] \Endereço_de_Instrução ,
  input  [1:0] R2,
  input  [1:0] R1,
  input  [7:0] Input,
  input  in_13,
  output [3:0] OP_CPU,
  output [7:0] out_15
);

  wire and_1_out, and_2_out, clear_2_out, clear_3_out, Clear_4_out, clear_out, Clock, not_1_out, not_2_out,
       not_3_out, ula_1_overflow, ula_1_zero, unidade_de_controle_1_alusrc, unidade_de_controle_1_branch,
       \unidade_de_controle_1_endereço , unidade_de_controle_1_jump, unidade_de_controle_1_memwrite_memread,
       unidade_de_controle_1_regwrite;
  wire [1:0] REG_1, REG_2, unidade_de_controle_1_memtoreg;
  wire [2:0] OP_ULA;
  wire [7:0] banco_de_registradores_1_reg_2_lido, INPUT_t, multiplexer_1_out, multiplexer_3_out, undriven;

  Clock clock_1 (.out(Clock));
  not not_1 (not_1_out, and_1_out);
  Counter counter_1 (
    .load(not_1_out), .D(INPUT_t), .count(and_1_out), .Q(\Endereço_de_Instrução ), .clk(Clock),
    .clr(clear_out));  // open: carry
  Button clear (.out(clear_out));
  RAM #(.dataWidth(16)) ram_1 (
    .addr(\Endereço_de_Instrução ), .data({OP_CPU, REG_2, REG_1, INPUT_t}), .clk(Clock), .clr(clear_2_out));  // open: sel, ld
  Button clear_2 (.out(clear_2_out));
  Multiplexer #(.select(2), .width(8), .enable("false")) multiplexer_1 (
    .in0(INPUT_t), .in1(ULA_S), .in2(undriven), .out(multiplexer_1_out), .sel(unidade_de_controle_1_memtoreg));  // open: in3
  and and_1 (and_1_out, not_3_out, not_2_out);
  Button clear_3 (.out(clear_3_out));
  Banco_de_Registradores banco_de_registradores_1 (
    .REG_1(REG_1), .REG_2(REG_2), .Esc_REG(unidade_de_controle_1_regwrite), .Input(multiplexer_1_out),
    .Clear(clear_3_out), .Clock(Clock), .REG_1_LIDO(ULA_A), .REG_2_LIDO(banco_de_registradores_1_reg_2_lido),
    .REG_00(REG_00), .REG_01(REG_01), .REG_10(REG_10), .REG_11(REG_11));
  Unidade_de_Controle unidade_de_controle_1 (
    .in_1(OP_CPU), .\Endereço (\unidade_de_controle_1_endereço ), .Jump(unidade_de_controle_1_jump),
    .Branch(unidade_de_controle_1_branch), .MemtoReg(unidade_de_controle_1_memtoreg), .ULAOP(OP_ULA),
    .MemWrite_MemRead(unidade_de_controle_1_memwrite_memread), .ALUSrc(unidade_de_controle_1_alusrc),
    .RegWrite(unidade_de_controle_1_regwrite));
  not not_2 (not_2_out, unidade_de_controle_1_jump);
  Multiplexer #(.width(8), .enable("false")) multiplexer_2 (
    .in0(banco_de_registradores_1_reg_2_lido), .in1(INPUT_t), .out(ULA_B), .sel(unidade_de_controle_1_alusrc));
  not not_3 (not_3_out, and_2_out);
  LED Overflow (.in(ula_1_overflow));
  and and_2 (and_2_out, unidade_de_controle_1_branch, ula_1_zero);
  ULA ula_1 (.A(ULA_A), .B(ULA_B), .Overflow(ula_1_overflow), .Zero(ula_1_zero), .OP_ULA(OP_ULA), .Output(ULA_S));
  Multiplexer #(.width(8), .enable("false")) multiplexer_3 (
    .in0(ULA_S), .in1(INPUT_t), .out(multiplexer_3_out), .sel(\unidade_de_controle_1_endereço ));
  \Memória_de_Dados  \memória_de_dados_1  (
    .Dado_Lido(undriven), .Dado_a_ser_Escrito(banco_de_registradores_1_reg_2_lido),
    .Seletor(multiplexer_3_out), .Enable_Seletor(unidade_de_controle_1_memwrite_memread), .Load(in_13),
    .Clear(Clear_4_out), .Clock(Clock));
  Button Clear_4 (.out(Clear_4_out));

  assign out_15 = ULA_S;

  // Other names for the same wires on the sheet: A[7:0] = ULA_A; B[7:0] = ULA_B;
  //   end_inst[7:0] = \Endereço_de_Instrução ; op_inst[3:0] = OP_CPU; reg_1_t[1:0] = R1; reg_2_t[1:0] = R2;
  //   S[7:0] = ULA_S

  // Notes on the sheet:
  //   000 ADD
  //   001 SUB
  //   010 AND
  //   011 NAND
  //   100 OR
  //   101 NOR
  //   110 XOR
  //   111 NOT
  //   0000 ADD
  //   0001 ADDI
  //   0010 SUB
  //   0011 SUBI
  //   0100 BEQ
  //   0101 JUMP
  //   0110 SW
  //   0111 LW
  //   1000 AND
  //   1001 NAND
  //   1010 OR
  //   1011 NOR
  //   1100 XOR
  //   1101 NOT
endmodule
